# Fritzing sketch potentiometre (saved by Fritzing 0.9.3b)
breadboards: 1

parts:
  U1 = ESP32S-HiLetgo [part_number=ESP32S-HiLetgo]
  LED1 = LED - 5mm [color="Red (633nm)" package="5 mm [THT]"]
  R2 = Rotary Potentiometer (Small) [maximum_resistance=100kΩ package=THT]
  R3 = Resistor [tolerance=±5% resistance=220 package="0402 [SMD]"]

nets:
  N1: U1.3.3, R2.leg1, R3.Pin_1
  N2: U1.GPIO14, R2.wiper
  N3: U1.GND, R2.leg2
  N4: U1.GPIO2, LED1.cathode
  N5: LED1.anode, R3.Pin_0

custom parts:
  ESP32S-HiLetgo: HiLetgo ESP-WROOM-32 ESP32 ESP-32S Development Board 2.4GHz Dual-Mode WiFi + Bluetooth Dual Cores Microcontroller The ESP32 integrated with Antenna switches, RF Balun, power amplifiers, low-noise amplifiers, filters, and management modules, and the entire solution occupies the least area of PCB. 2.4 GHz Wi-Fi plus Bluetooth dual-mode chip, with TSMC Ultra-low power consumption 40nm technology,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
